# Fritzing sketch Untitled Sketch (saved by Fritzing 0.9.2b)
breadboards: 1

parts:
  D1 = LED_BARGRAPH_10 [package=led_bargaph_10]
  S1 = Momentary Switch [package=ksa_sealed_tac_switch]
  LED7 = LEDs [package=led10mm]
  Parte1 = Arduino ProtoScrew Shield Kit  # not connected
  Parte2 = Arduino ProtoScrew Shield Kit
  U15 = 3.5mm Audio Jack [package=audio-jack-3.5mm-smd]  # not connected
  X1 = DB9 Connector [package=db9]  # not connected
  X2 = DB9 Connector [package=db9]  # not connected
  LED8 = Super Flux LED blue [color=Blue]  # not connected
  LED9 = Super Flux LED blue [color=Blue]
  LED10 = Super Flux LED blue [color=Blue]
  LED11 = Super Flux LED blue [color=Blue]
  S4 = Momentary Switch [package=ksa_sealed_tac_switch]  # not connected
  S5 = Momentary Switch [package=ksa_sealed_tac_switch]  # not connected
  S6 = Momentary Switch [package=ksa_sealed_tac_switch]  # not connected
  S7 = Momentary Switch [package=ksa_sealed_tac_switch]  # not connected
  SW1 = DIP SWITCH [package=dipswitch-02]  # not connected
  SW2 = DIP SWITCH [package=dipswitch-02]  # not connected
  U20 = SWITCH_SPDT [package=kps-1290]  # not connected
  LED12 = Super Flux LED blue [color=Blue]  # not connected
  LED13 = Super Flux LED blue [color=Blue]  # not connected
  LED14 = Super Flux LED blue [color=Blue]  # not connected
  LED15 = Super Flux LED blue [color=Blue]  # not connected
  LED16 = Super Flux LED blue [color=Blue]  # not connected
  LED17 = Super Flux LED blue [color=Blue]  # not connected
  U21 = ATTINY13 [package=dip]  # not connected
  U22 = ATTINY45 [package=dip]  # not connected
  U23 = RS232 Transceiver [package=dil16]  # not connected
  U30 = KENT_LCD_CONN [package=ffc_16]  # not connected
  U31 = KENT_LCD_CONN [package=ffc_16]  # not connected
  U32 = OP37 - Low Noise, Precision, High Speed Op Amp [part_number=OP37]  # not connected
  IC1 = L293D [package=THT]  # not connected
  U33 = Graphical LCD 128x64 [package=1x20]  # not connected
  R2 = Resistor [tolerance=±5% resistance=220 package=THT]
  R3 = Resistor [tolerance=±5% resistance=220 package=THT]
  R5 = Resistor [tolerance=±5% resistance=220 package=THT]
  R7 = Resistor [tolerance=±5% resistance=220 package=THT]
  R8 = Resistor [tolerance=±5% resistance=220 package=THT]
  R9 = Resistor [tolerance=±5% resistance=220 package=THT]
  R10 = Resistor [tolerance=±5% resistance=220 package=THT]
  S8 = Momentary Switch [package=ksa_sealed_tac_switch]
  LED18 = LEDs [package=led10mm]
  R11 = Resistor [tolerance=±5% resistance=220 package=THT]
  R12 = Resistor [tolerance=±5% resistance=220 package=THT]
  RFID1 = RFID Reader  # not connected
  S9 = Momentary Switch [package=ksa_sealed_tac_switch]
  R13 = Resistor [tolerance=±5% resistance=220 package=THT]
  R14 = Resistor [tolerance=±5% resistance=220 package=THT]
  R15 = Resistor [tolerance=±5% resistance=220 package=THT]
  U34 = Graphical LCD 128x64 [package=1x20]  # not connected
  R16 = RPACK* [package=rpack-sip-pth-5]
  R17 = RPACK* [package=rpack-sip-pth-5]  # not connected
  R18 = RPACK* [package=rpack-sip-pth-5]  # not connected
  R19 = RPACK* [package=rpack-sip-pth-5]  # not connected
  R20 = RPACK* [package=rpack-sip-pth-5]  # not connected
  R21 = RPACK* [package=rpack-sip-pth-5]
  R22 = RPACK* [package=rpack-sip-pth-5]
  R23 = RPACK* [package=rpack-sip-pth-5]
  R24 = RPACK* [package=rpack-sip-pth-5]  # not connected
  R25 = RPACK* [package=rpack-sip-pth-5]  # not connected
  R26 = RPACK* [package=rpack-sip-pth-5]  # not connected
  R27 = RPACK* [package=rpack-sip-pth-5]  # not connected
  R28 = RPACK* [package=rpack-sip-pth-5]  # not connected
  R29 = RPACK* [package=rpack-sip-pth-5]  # not connected
  R32 = Rotary Potentiometer (Small) [maximum_resistance=100kΩ package=THT]  # not connected
  U35 = RF24G Header [package=rf24g-2x5]  # not connected

nets:
  N1: D1.A_A, R23.1
  N2: D1.B_A, R22.1
  N3: D1.C_A, R23.2
  N4: D1.D_A, R22.2
  N5: D1.E_A, R23.3
  N6: D1.F_A, R22.3
  N7: D1.G_A, R23.4
  N8: D1.H_A, R22.4
  N9: D1.I_A, R23.5
  N10: D1.J_A, R22.5
  N11: D1.J_C, R10.Pin_1
  N12: D1.I_C, R9.Pin_1
  N13: D1.H_C, R8.Pin_1
  N14: D1.G_C, R15.Pin_1
  N15: D1.F_C, R7.Pin_1
  N16: D1.E_C, R5.Pin_1
  N17: D1.D_C, R14.Pin_1
  N18: D1.C_C, R3.Pin_1
  N19: D1.B_C, R2.Pin_1
  N20: D1.A_C, R13.Pin_1
  N21: S1.3, R2.Pin_0, R3.Pin_0, R5.Pin_0, R7.Pin_0, R8.Pin_0, R9.Pin_0, R10.Pin_0, S8.3, R11.Pin_1, R12.Pin_1, S9.1, R13.Pin_0, R14.Pin_0, R15.Pin_0
  N22: S1.4, R16.1
  N23: LED7.A, R21.2
  N24: LED7.C, R11.Pin_0
  N25: Parte2.GND, LED11.anode
  N26: Parte2.D8, LED9.anode
  N27: Parte2.D10, LED9.cathode
  N28: Parte2.D11, LED10.anode
  N29: Parte2.D13, LED10.cathode
  N30: S8.4, R21.1
  N31: LED18.A, R16.2
  N32: LED18.C, R12.Pin_0
  N33: S9.4, R21.4
